// Logisim project CPU01.circ as structural Verilog: 5 circuits, main circuit flip-flop alterado
module flip_flop_alterado (
  input  JMP,
  input  END,
  input  CLK,
  input  Entrada,
  input  CLR,
  output Q,
  output Q_prime
);

  wire and_1_out, and_2_out, or_1_out;

  and and_1 (and_1_out, JMP, END);
  and and_2 (and_2_out, ~CLR, or_1_out);  // AND_Gate
  T_Flip_Flop #(.trigger("falling"), .NegatePresetClear("true")) t_ff_1 (
    .clk(CLK), .T(Entrada), .Q(Q), .Qn(Q_prime), .preset(and_1_out), .reset(and_2_out));
  or or_1 (or_1_out, ~JMP, END);  // OR_Gate
endmodule

module contador (
  input  [3:0] Endereco,
  input  CLK,
  input  JUMP,
  input  Master_CLR,
  output [7:0] out_5
);

  wire and_1_out, and_2_out, and_3_out, and_4_out, and_5_out, and_6_out;

  flip_flop_alterado flip_flop_alterado_1 (
    .CLK(CLK), .Entrada(1'b1), .JMP(JUMP), .END(Endereco[0]), .CLR(Master_CLR), .Q(out_5[0]));  // open: Q_prime
  flip_flop_alterado flip_flop_alterado_2 (
    .CLK(CLK), .Entrada(out_5[0]), .JMP(JUMP), .END(Endereco[1]), .CLR(Master_CLR), .Q(out_5[1]));  // open: Q_prime
  and and_1 (and_1_out, out_5[1], out_5[0]);
  flip_flop_alterado flip_flop_alterado_3 (
    .CLK(CLK), .Entrada(and_1_out), .JMP(JUMP), .END(Endereco[2]), .CLR(Master_CLR), .Q(out_5[2]));  // open: Q_prime
  and and_2 (and_2_out, out_5[2], and_1_out);
  Hex_Digit_Display hex_digit_display_1 (.value(out_5[7:4]));  // open: dp
  flip_flop_alterado flip_flop_alterado_4 (
    .CLK(CLK), .Entrada(and_2_out), .JMP(JUMP), .END(Endereco[3]), .CLR(Master_CLR), .Q(out_5[3]));  // open: Q_prime
  and and_3 (and_3_out, out_5[3], and_2_out);
  Hex_Digit_Display hex_digit_display_2 (.value(out_5[3:0]));  // open: dp
  flip_flop_alterado flip_flop_alterado_5 (
    .CLK(CLK), .Entrada(and_3_out), .JMP(JUMP), .END(1'b0), .CLR(Master_CLR), .Q(out_5[4]));  // open: Q_prime
  and and_4 (and_4_out, out_5[4], and_3_out);
  flip_flop_alterado flip_flop_alterado_6 (
    .CLK(CLK), .Entrada(and_4_out), .JMP(JUMP), .END(1'b0), .CLR(Master_CLR), .Q(out_5[5]));  // open: Q_prime
  and and_5 (and_5_out, out_5[5], and_4_out);
  flip_flop_alterado flip_flop_alterado_7 (
    .CLK(CLK), .Entrada(and_5_out), .JMP(JUMP), .END(1'b0), .CLR(Master_CLR), .Q(out_5[6]));  // open: Q_prime
  and and_6 (and_6_out, out_5[6], and_5_out);
  flip_flop_alterado flip_flop_alterado_8 (
    .CLK(CLK), .Entrada(and_6_out), .JMP(JUMP), .END(1'b0), .CLR(Master_CLR), .Q(out_5[7]));  // open: Q_prime

  // Other names for the same wires on the sheet: E0 = Endereco[0]; E1 = Endereco[1]; E2 = Endereco[2];
  //   E3 = Endereco[3]
endmodule

module main (
);

  wire JUMP, K0, K1, K2, K3, L0, L1, L2, L3, L4, L5, L6, L7, L8, L9, S0, S1, S2, S3, S4, S5, S6, S7, S8, S9;
  wire [1:0] divisorbits_1_jump;
  wire [3:0] HEX0, HEX1, HEX2, HEX3, HEX4, HEX5, Operando;

  Hex_Digit_Display hex_digit_display_1 (.value(HEX5));  // open: dp
  LED u_L8 (.in(L8));
  LED u_L9 (.in(L9));
  // DipSwitch #(.NSwitches(1)) S8: pin names not known; wires that end beside it: S8
  // DipSwitch #(.NSwitches(1)) S9: pin names not known; wires that end beside it: S9
  Hex_Digit_Display hex_digit_display_2 (.value(HEX3));  // open: dp
  Hex_Digit_Display hex_digit_display_3 (.value(HEX4));  // open: dp
  LED u_L7 (.in(L7));
  LED u_L5 (.in(L5));
  LED u_L6 (.in(L6));
  // DipSwitch #(.NSwitches(1)) S6: pin names not known; wires that end beside it: S6
  // DipSwitch #(.NSwitches(1)) S7: pin names not known; wires that end beside it: S7
  // DipSwitch #(.NSwitches(1)) S5: pin names not known; wires that end beside it: S5
  contador Contador (
    .Endereco(Operando), .CLK(S9), .JUMP(S9), .Master_CLR(S0), .out_5({L7, L6, L5, L4, L3, L2, L1, L0}));
  Hex_Digit_Display hex_digit_display_4 (.value(HEX2));  // open: dp
  LED u_L4 (.in(L4));
  LED u_L3 (.in(L3));
  // DipSwitch #(.NSwitches(1)) S2: pin names not known; wires that end beside it: S2
  // DipSwitch #(.NSwitches(1)) S3: pin names not known; wires that end beside it: S3
  // DipSwitch #(.NSwitches(1)) S4: pin names not known; wires that end beside it: S4
  Hex_Digit_Display hex_digit_display_5 (.value(HEX1));  // open: dp
  Hex_Digit_Display hex_digit_display_6 (.value(HEX0));  // open: dp
  LED u_L2 (.in(L2));
  LED u_L0 (.in(L0));
  LED u_L1 (.in(L1));
  // DipSwitch #(.NSwitches(1)) S1: pin names not known; wires that end beside it: S1
  // DipSwitch #(.NSwitches(1)) S0: pin names not known; wires that end beside it: S0
  Button u_K2 (.out(K2));
  Button u_K3 (.out(K3));
  Button u_K0 (.out(K0));
  Button u_K1 (.out(K1));
  // Digital_Oscilloscope #(.nState(16)) digital_oscilloscope_1: pin names not known; wires that end beside it: S9, L0, L1, L2, L3, L4, L5, L6, L7
  ROM #(.dataWidth(16), .Select("low")) rom_1 (
    .addr({L7, L6, L5, L4, L3, L2, L1, L0}), .data({HEX5, HEX4, HEX3, HEX2}));
  divisorBits divisorbits_1 (
    .in_1({HEX5, HEX4, HEX3, HEX2}), .\Disponível (Operando), .JUMP(divisorbits_1_jump));  // open: Operando, RgTO, RgTIn, ULA
  and and_1 (JUMP, divisorbits_1_jump[0], divisorbits_1_jump[1]);

  // Notes on the sheet:
  //   contents of rom_1 (hex, n*v repeats v):
  //   6005 9101 6202 6304 c08 0 0 0 400 6001 9001 9002 6302 6102 9302 6200 6001 800
endmodule

module divisorBits (
  input  [15:0] in_1,
  output [3:0] Operando,
  output [3:0] \Disponível ,
  output [1:0] ULA,
  output [1:0] JUMP,
  output [1:0] RgTO,
  output [1:0] RgTIn
);


  assign \Disponível  = in_1[7:4];
  assign JUMP = in_1[11:10];
  assign Operando = in_1[3:0];
  assign RgTIn = in_1[13:12];
  assign RgTO = in_1[15:14];
  assign ULA = in_1[9:8];
endmodule

module MemoriaROM (
);

  ROM #(.dataWidth(16), .Select("low")) rom_1 ();  // open: addr, data

  // Notes on the sheet:
  //   contents of rom_1 (hex, n*v repeats v):
  //   6005 9101 6202 6304 c08 0 0 0 400 6001 9001 9002 6302 6102 9302 6200 6001 800
endmodule
